# Fritzing sketch Oscilloscope(Arduino) (saved by Fritzing 0.9.3b)
breadboards: 1

parts:
  Arduino_UNO = Arduino Uno (Rev3)
  R2 = Resistor [tolerance=±5% resistance=1k package=THT]
  R3 = Resistor [tolerance=±5% resistance=15k package=THT]
  LED2 = LED - 3mm [color="Blue (525nm)" package="3 mm [THT]"]
  R4 = Resistor [tolerance=±5% resistance=60k package=THT]

nets:
  N1: Arduino_UNO.A0, R3.Pin_1, R4.Pin_0
  N2: Arduino_UNO.D8, R2.Pin_1
  N3: Arduino_UNO.GND, R3.Pin_0, LED2.cathode
  N4: R2.Pin_0, LED2.anode

notes:
  Probe CH1 +
  Probe
  CH1 - (Gnd)
  Measure (0-25)V DC
  to 0-1024 ADC values
