# Fritzing sketch Oscilloscope(OnRaster) (saved by Fritzing 0.9.3b)
breadboards: 1

parts:
  U1 = atmega328 [package=dip]
  Εξάρτημα1 = Arduino Uno (Rev3)
  Y1 = CRYSTAL [package=hc49us]
  C1 = Capacitor [package=cap-pth-small2]
  C2 = Capacitor [package=cap-pth-small2]
  R2 = Resistor [tolerance=±5% resistance=1k package=THT]
  R3 = Resistor [tolerance=±5% resistance=15k package=THT]
  LED2 = LED - 3mm [color="Blue (525nm)" package="3 mm [THT]"]
  R4 = Resistor [tolerance=±5% resistance=60k package=THT]
  R5 = Resistor [tolerance=±5% resistance=10k package="2010 [SMD]"]

nets:
  N1: U1.RESET, Εξάρτημα1.RESET, R5.Pin_0
  N2: U1.D0_(RX), Εξάρτημα1.D0/RX
  N3: U1.D1_(TX), Εξάρτημα1.D1/TX
  N4: U1.VCC, R5.Pin_1
  N5: U1.GND#7, LED2.anode
  N6: U1.XLAT1, Y1.2, C2.1
  N7: U1.XLAT2, Y1.1, C1.2
  N8: U1.D8, R2.Pin_0
  N9: U1.AVCC, U1.AREF, Εξάρτημα1.5V
  N10: U1.GND#21, Εξάρτημα1.GND, C1.1, C2.2, R3.Pin_0
  N11: U1.A0, R3.Pin_1, R4.Pin_0
  N12: R2.Pin_1, LED2.cathode

notes:
  Probe CH1 +
  Probe
  CH1 - (Gnd)
  Measure (0-25)V DC
  to 0-1024 ADC values
